# Fritzing sketch Gassensor (saved by Fritzing 0.9.3b)
circuit board: 8.46667cm x 5.64444cm
breadboards: 1

parts:
  LCD1 = LCD screen
  Bauteil1 = Arduino Nano (Rev3.0)
  Bauteil2 = MQ-135 breakout  # not connected
  U1 = POT [package=pot_alpha_rv16af-20]

nets (from the breadboard view):
  VSS: LCD1.VSS, LCD1.R/W, LCD1.LED-, Bauteil1.GND, U1.A
  VDD: LCD1.VDD, LCD1.LED+, Bauteil1.VIN, U1.E
  N1: LCD1.V0, U1.S
  N2: LCD1.RS, Bauteil1.D12/MISO
  N3: LCD1.E, Bauteil1.D11/MOSI
  N4: LCD1.DB4, Bauteil1.D5
  N5: LCD1.DB5, Bauteil1.D4
  N6: LCD1.DB6, Bauteil1.D3
  N7: LCD1.DB7, Bauteil1.D2
